# Fritzing sketch FakeSecurity (saved by Fritzing 0.9.3b)
breadboards: 1

parts:
  LED1 = LED - 3mm [color="Red (633nm)" package="3 mm [THT]"]
  LED2 = LED - 3mm [color="Blue (470nm)" package="3 mm [THT]"]
  WeMos_D1_Mini1 = WeMos D1 Mini
  R1 = Resistor [tolerance=±5% resistance=100 package=THT]
  R2 = Resistor [tolerance=±5% resistance=100 package=THT]

nets:
  N1: LED1.cathode, R2.Pin_1
  N2: LED1.anode, WeMos_D1_Mini1.D6
  N3: LED2.cathode, R1.Pin_1
  N4: LED2.anode, WeMos_D1_Mini1.D5
  N5: WeMos_D1_Mini1.G, R1.Pin_0, R2.Pin_0
